# Fritzing sketch LiveLights Remote (saved by Fritzing 0.8.7b)
breadboards: 1

parts:
  xbee1 = artuino [part_number=126]
  Power_RGB3 = Prolight RGB 3 Watt Star
  Part1 = Arduino Uno (Rev3)
  JACK1 = 2.1mm Barrel Jack with Terminal Block
  Q1 = TIP120 Hi-Current Darlington Transistor
  Q2 = TIP120 Hi-Current Darlington Transistor
  Q3 = TIP120 Hi-Current Darlington Transistor
  R1 = Resistor [tolerance=±5% resistance=1k package=THT]
  R2 = Resistor [tolerance=±5% resistance=1k package=THT]
  R3 = Resistor [tolerance=±5% resistance=1k package=THT]

nets:
  N1: xbee1.3v#1, Part1.3V3
  GND: xbee1.gnd, Part1.GND, JACK1.NEG, Q1.EMITTER, Q2.EMITTER, Q3.EMITTER
  N2: xbee1.rx, Part1.D3_PWM
  N3: xbee1.tx, Part1.D2
  N4: Power_RGB3.B+, Power_RGB3.G+, Power_RGB3.R+, Part1.VIN, JACK1.POS
  N5: Power_RGB3.R-, Q1.COLLECTOR
  N6: Power_RGB3.G-, Q2.COLLECTOR
  N7: Power_RGB3.B-, Q3.COLLECTOR
  N8: Part1.D9_PWM, R1.Pin_1
  N9: Part1.D10_PWM/SS, R2.Pin_1
  N10: Part1.D11_PWM/MOSI, R3.Pin_1
  N11: Q1.BASE, R3.Pin_0
  N12: Q2.BASE, R2.Pin_0
  N13: Q3.BASE, R1.Pin_0

notes:
  9v Wall Charger

custom parts:
  artuino: Adafruit Xbee Adapter
